# Fritzing sketch led_childroom (saved by Fritzing 0.9.3b)
breadboards: 1

parts:
  U1 = NodeMCU V3.0
  M1 = RioRand LM2596
  Power_supply_12v_5A = Power plug
  470uf = Capacitor Polarized [package=cpol-radial-100uf-25v]
  220uf = Capacitor Polarized [package=cpol-radial-100uf-25v]
  R3 = Resistor [tolerance=±5% resistance=1k package="2010 [SMD]"]
  S8550 = PNP-Transistor [package="TO92 [THT]"]
  R4 = Resistor [tolerance=±5% resistance=3.3k package="2010 [SMD]"]
  LED1 = DUO LED RG [package="5 mm [THT]"]

nets:
  N1: U1.D4, R4.Pin_0
  N2: U1.GND#6, U1.GND#13, U1.GND#16, U1.GND#33, M1.Pin_4, 220uf.-
  N3: U1.Vin, M1.Pin_3, 220uf.+, R3.Pin_1
  N4: M1.Pin_1, Power_supply_12v_5A.VCC, 470uf.+, LED1.green_anode
  N5: M1.Pin_2, Power_supply_12v_5A.GND, 470uf.-, S8550.E, LED1.red_anode
  N6: R3.Pin_0, S8550.C, LED1.common_cathode
  N7: S8550.B, R4.Pin_1

notes:
  12v
  5v
  WS2811 led strip 12v

custom parts:
  NodeMCU V3.0: ESP8266 based NodeMCU
